# Fritzing sketch ESP32-MQTT-Weather-windSpeed (saved by Fritzing 1.0.5)

parts:
  M1 = DOIT Esp32 DevKit v1 (30 pins long, 11 pins width) [part_number=ESP32S-PIN30]
  M2 = MAX485 Breakout [package=THT]
  Wind_Speed_Sensor_PR-3000-FSJT-N1 = Wind Speed Sensor PR-3000-FSJT-N01
  V1_12V = DC Power Supply [voltage=12V internal_resistance=1Ω max_current=0.1A]
  U1 = DC-DC_CONVERTER [package=dc-dc_converter]

nets:
  3V3: M1.3V3, M2.VCC
  GND: M1.GND, M2.GND, Wind_Speed_Sensor_PR-3000-FSJT-N1.GND, V1_12V.Pin_1, U1.VOUT, U1.GND2
  N1: M1.D4, M2.RE, M2.DE
  N2: M1.RX2, M2.RO
  N3: M1.TX2, M2.DI
  N4: M1.VIN, U1.SENSE
  N5: M2.A, Wind_Speed_Sensor_PR-3000-FSJT-N1.485_A+
  N6: M2.B, Wind_Speed_Sensor_PR-3000-FSJT-N1.485_B-
  N7: Wind_Speed_Sensor_PR-3000-FSJT-N1.Power_10-30V, V1_12V.Pin_2, U1.TRIM

custom parts:
  DOIT Esp32 DevKit v1 (30 pins long, 11 pins width): The DOIT Esp32 DevKit v1 is one of the development board created by DOIT to evaluate the ESP-WROOM-32 module. It is based on the ESP32 microcontroller that boasts Wifi, Bluetooth, Ethernet and Low Power support all in a single chip. (vanepp) made breadboard work, adjusted pin numbering and labels and reduced size of schematic and cleaned up pcb. This chip is 30pins long (2 x15) and 11 pins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
  MAX485 Breakout: MAX485 RS485 breakout board
